# Fritzing sketch FlightSystemTestWiring (saved by Fritzing 0.9.3b)
breadboards: 1

parts:
  SMA_Antenna_Connector1 = SMA Antenna Connector [package=sma-edge]
  Teensy_3_6 = Teensy 3.6 (Basic)
  LoRa_Radio1 = Adafruit RFM9x LoRa Radio [part_number="Adafruit #3072 and #3073"]
  GPS1 = Adafruit Ultimate GPS v3 [part_number="Adafruit #746"]
  Battery = Battery Holders [package=lipo-1100mAh]

nets:
  N1: SMA_Antenna_Connector1.GND, LoRa_Radio1.ANTENNA
  GND: Teensy_3_6.GND, Teensy_3_6.GND1, LoRa_Radio1.GND, GPS1.GND, Battery.-
  N2: Teensy_3_6.D2, LoRa_Radio1.RST
  N3: Teensy_3_6.D3, LoRa_Radio1.DIO0
  N4: Teensy_3_6.D4, LoRa_Radio1.CS
  N5: Teensy_3_6.D7, GPS1.TX
  N6: Teensy_3_6.D8, GPS1.RX
  N7: Teensy_3_6.D11, LoRa_Radio1.MOSI
  N8: Teensy_3_6.D12, LoRa_Radio1.MISO
  N9: Teensy_3_6.D13, LoRa_Radio1.SCK
  VIN: Teensy_3_6.Vin, LoRa_Radio1.VIN, GPS1.VIN, Battery.+

custom parts:
  Teensy 3.6 (Basic): The Teensy is a complete USB-based microcontoller development system, in a very small footprint, capable of implementing many types of projects. All programming is done via the USB port. No special programmer is needed, only a standard micro-USB cable and a PC or Macintosh with a USB port.
  Adafruit RFM9x LoRa Radio: Sending data over long distances is like magic, and now you can be a magician with this range of powerful and easy-to-use radio modules. Sure, sometimes you want to talk to a computer (a good time to use WiFi) or perhaps communicate with a Phone (choose Bluetooth Low Energy!) but what if you want to send data very far? Most WiFi, Bluetooth, Zigbee and other wireless chipsets use 2.4GHz, which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
  Adafruit Ultimate GPS v3: We carry a few different GPS modules here in the Adafruit shop, but none that satisfied our every desire - that's why we designed this little GPS breakout board. We believe this is the Ultimate GPS module, so we named it that. It's got everything you want and more: -165 dBm sensitivity, 10 Hz updates, 66 channels 5V friendly design and only 20mA current draw Breadboard friendly + two mounting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
