# Fritzing sketch GroundSystemTestWiring (saved by Fritzing 0.9.3b)
breadboards: 1

parts:
  - = Battery Holders [package=lipo-1100mAh]
  GND_TX = Adafruit RFM9x LoRa Radio [part_number="Adafruit #3072 and #3073"]
  GND_MCU = Arduino Uno (Rev3)
  GND_ANT = HC-12 Antenna

nets:
  N1: -.+, GND_MCU.VIN
  N2: -.-, GND_TX.GND
  N3: GND_TX.ANTENNA, GND_ANT.ANT
  VIN: GND_TX.VIN, GND_MCU.5V
  N4: GND_TX.DIO0, GND_MCU.D3_PWM
  N5: GND_TX.SCK, GND_MCU.D13/SCK
  N6: GND_TX.MISO, GND_MCU.D12/MISO
  N7: GND_TX.MOSI, GND_MCU.D11_PWM/MOSI
  N8: GND_TX.CS, GND_MCU.D4
  N9: GND_TX.RST, GND_MCU.D2

custom parts:
  Adafruit RFM9x LoRa Radio: Sending data over long distances is like magic, and now you can be a magician with this range of powerful and easy-to-use radio modules. Sure, sometimes you want to talk to a computer (a good time to use WiFi) or perhaps communicate with a Phone (choose Bluetooth Low Energy!) but what if you want to send data very far? Most WiFi, Bluetooth, Zigbee and other wireless chipsets use 2.4GHz, which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
  HC-12 Antenna: Antenna for HC-12 433Mhz Module
